# Fritzing sketch obstacle_avoidance (saved by Fritzing 0.8.7b)
breadboards: 1

parts:
  Ultrasonic_Sensor = SRF05 Ultrasonic Rangefinder
  Part2 = Arduino Uno (Rev3)
  M1 = DC Motor
  Right_Motor = DC Motor
  S1 = H-Bridge with L298N
  VCC1 = Battery

nets:
  VCC: Ultrasonic_Sensor.VCC, S1.5V
  N1: Ultrasonic_Sensor.Trig, Part2.A3
  N2: Ultrasonic_Sensor.Echo, Part2.A2
  GND: Ultrasonic_Sensor.GND, Part2.GND, S1.GND, VCC1.-
  N3: Part2.D10_PWM/SS, S1.IN3
  N4: Part2.D11_PWM/MOSI, S1.IN4
  N5: Part2.D12/MISO, S1.IN2
  N6: Part2.D13/SCK, S1.IN1
  N7: M1.pin_1, S1.M1-02
  N8: M1.pin_2, S1.M1-01
  N9: Right_Motor.pin_1, S1.M2-02
  N10: Right_Motor.pin_2, S1.M2-01
  N11: S1.12V, VCC1.+

custom parts:
  H-Bridge with L298N: h-bridge
